# Fritzing sketch coffeeboxcounter (saved by Fritzing 0.9.3b)

parts:
  WeMos_D1_Mini1 = WeMos D1 Mini
  WeMos_D1_Mini_OLED_Shield1 = WeMos D1 Mini OLED Shield
  S1 = Round Pushbutton
  J1 = Piezo Speaker
  SG1 = Buzzer 12mm [package=buzzer-cmt1102]  # not connected

nets:
  3V3: WeMos_D1_Mini1.3V3, WeMos_D1_Mini_OLED_Shield1.3V3, S1.leg1
  N1: WeMos_D1_Mini1.D0, S1.leg0
  N2: WeMos_D1_Mini1.D1, WeMos_D1_Mini_OLED_Shield1.D1
  N3: WeMos_D1_Mini1.D2, WeMos_D1_Mini_OLED_Shield1.D2
  N4: WeMos_D1_Mini1.D4, J1.pin2
  N5: WeMos_D1_Mini1.G, WeMos_D1_Mini_OLED_Shield1.G, J1.pin1
